# Fritzing sketch MCU (saved by Fritzing 0.9.3b)
breadboards: 1

parts:
  Part1 = Arduino Uno (Rev3) - ICSP
  MS5803-14BA1 = MS5803-14BA Pressure Sensor
  Part2 = Logic Level Converter
  R1 = Resistor [tolerance=±5% resistance=220 package="0603 [SMD]"]
  R2 = Resistor [tolerance=±5% resistance=560 package="2512 [SMD]"]
  R3 = Resistor [tolerance=±5% resistance=1.7k package="2512 [SMD]"]
  R4 = Resistor [tolerance=±5% resistance=4.7k package="2512 [SMD]"]
  R5 = Resistor [tolerance=±5% resistance=10k package="2512 [SMD]"]
  R6 = Resistor [tolerance=±5% resistance=10k package="2512 [SMD]"]
  S1 = Pushbutton [package="[THT]"]
  S2 = Pushbutton [package="[THT]"]
  S3 = Pushbutton [package="[THT]"]
  S4 = Pushbutton [package="[THT]"]
  S5 = Pushbutton [package="[THT]"]
  R7 = Resistor [tolerance=±5% resistance=10k package="0603 [SMD]"]
  R8 = Resistor [tolerance=±5% resistance=10k package="0603 [SMD]"]
  C1 = Ceramic Capacitor [capacitance=100nF package="200 mil [THT, multilayer]"]
  Part3 = GUVA-S12SD UV Light Sensor
  Grove1 = Grove RGB LCD 2 x 16

nets:
  N1: Part1.A2, Part3.Out
  N2: Part1.A3, R6.Pin_0, S1.Pin_3, S1.Pin_4, S2.Pin_3, S2.Pin_4, S3.Pin_3, S3.Pin_4, S4.Pin_3, S4.Pin_4, S5.Pin_3, S5.Pin_4
  N3: Part1.A4/SDA, Part2.RX_HV, R8.Pin_1, Grove1.SDA
  N4: Part1.A5/SCL, Part2.TX_HV, Grove1.SCL
  N5: Part1.3V3, Part2.LV, C1.1
  5V: Part1.5V, Part2.HV, R1.Pin_1, R2.Pin_1, R3.Pin_1, R4.Pin_1, R5.Pin_1, Part3.5V, Grove1.VCC
  GND: Part1.GND, MS5803-14BA1.GND, Part2.GND, R6.Pin_1, R7.Pin_0, R8.Pin_0, C1.0, Part3.GND, Grove1.GND
  N6: MS5803-14BA1.SCL, Part2.TX_LV, R7.Pin_1
  N7: MS5803-14BA1.SDA, Part2.RX_LV
  N8: R1.Pin_0, S1.Pin_1, S1.Pin_2
  N9: R2.Pin_0, S2.Pin_1, S2.Pin_2
  N10: R3.Pin_0, S3.Pin_1, S3.Pin_2
  N11: R4.Pin_0, S4.Pin_1, S4.Pin_2
  N12: R5.Pin_0, S5.Pin_1, S5.Pin_2

custom parts:
  MS5803-14BA Pressure Sensor: MS5803-14BA pressure sensor by Measurement Specialities Connects over I2C or SPI
  GUVA-S12SD UV Light Sensor: Extend your light-sensing spectrum with this analog UV sensor module. It uses a UV photodiode, which can detect the 240-370nm range of light (which covers UVB and most of UVA spectrum). The signal level from the photodiode is very small, in the nano-ampere level, so we tossed on an opamp to amplify the signal to a more manageable volt-level.
  Grove RGB LCD 2 x 16: Grove RGB LCD - 2 x 16 from Seeed studio starter kit
