# Fritzing sketch NEMA_17_DRV8825 (saved by Fritzing 0.9.3b)
breadboards: 1

parts:
  Arduino_UNO = Arduino Uno (Rev3)
  Power_plug_12V_3A = Power plug
  DRV_8825 = DRV 8825 Stepper Motor Carrier, High Current
  100μF_16V_capacitor = Electrolytic Capacitor [package="100 mil [THT, electrolytic]"]  # not connected
  NEMA17_350_mA_12_V1 = Stepper Motor - Bipolar

nets (from the schematic view):
  N1: Arduino_UNO.D3_PWM, DRV_8825.STEP
  N2: Arduino_UNO.D6_PWM, DRV_8825.DIRECTION
  N3: Arduino_UNO.5V, DRV_8825.RESET, DRV_8825.SLEEP
  N4: Arduino_UNO.GND, DRV_8825.GROUND_LOG
  N5: Power_plug_12V_3A.GND, DRV_8825.GROUND_ST/_MT
  N6: Power_plug_12V_3A.VCC, DRV_8825.VOLTAGE_ST/_MT
  N7: DRV_8825.OUT_2B, NEMA17_350_mA_12_V1.A
  N8: DRV_8825.OUT_2A, NEMA17_350_mA_12_V1.C
  N9: DRV_8825.OUT_1A, NEMA17_350_mA_12_V1.B
  N10: DRV_8825.OUT_1B, NEMA17_350_mA_12_V1.D

custom parts:
  Electrolytic Capacitor: A small electrolytic capacitor
  Stepper Motor - Bipolar: Simple, but very powerful bi polar stepper motor. 4 wire. NEMA17.
